// Logisim project processador.circ as structural Verilog: 4 circuits, main circuit main
module main (
  input  in_1,
  input  in_2
);

  wire and_1_out, bge, Branch, clock_1_out, DoI, Jump, li, MemRead, multiplexer_3_out, or_1_out, RegWrit,
       ula_1_igual, ula_1_maior, unidadecontrole_1_memorula, unidadecontrole_1_memstore;
  wire [2:0] functCtrl;
  wire [3:0] demultiplexer_1_out0, demultiplexer_1_out1, multiplexer_1_out, Opcode, R0, R1, R2;
  wire [15:0] adder_1_out, bit_extender_1_out, multiplexer_2_out, multiplexer_5_out, PC_q, ram_1_data,
       Registradores_read_data_1, Registradores_read_data_2, ula_1_r, WriteData;

  Register #(.width(16)) PC (.D(multiplexer_5_out), .Q(PC_q), .clk(clock_1_out), .clr(in_2));  // open: en
  Adder #(.width(16)) adder_1 (.a(16'h1), .b(PC_q), .out(adder_1_out));  // open: cin, cout
  ROM #(.addrWidth(16), .dataWidth(16)) rom_1 (.addr(PC_q), .data({Opcode, R0, R1, R2}));  // open: sel
  Demultiplexer #(.width(4), .enable("false")) demultiplexer_1 (
    .out0(demultiplexer_1_out0), .out1(demultiplexer_1_out1), .in(R2), .sel(li));
  Clock clock_1 (.out(clock_1_out));
  Multiplexer #(.width(4), .enable("false")) multiplexer_1 (
    .in0(demultiplexer_1_out1), .in1(R0), .out(multiplexer_1_out), .sel(DoI));
  UnidadeControle unidadecontrole_1 (
    .a(Opcode[3]), .b(Opcode[2]), .c(Opcode[1]), .d(Opcode[0]), .MemStore(unidadecontrole_1_memstore),
    .RegWrite(RegWrit), .MemOrULA(unidadecontrole_1_memorula), .J(Jump), .Branch(Branch),
    .functCtrl1(functCtrl[0]), .functCtrl2(functCtrl[1]), .functCtrl3(functCtrl[2]), .MemRead(MemRead),
    .li(li), .bge(bge), .DestinoOuImediato(DoI));
  registradores Registradores (
    .Read_reg_1(multiplexer_1_out), .Read_reg_2(R1), .Write_data(WriteData), .Write_reg(R0),
    .RegWrite(RegWrit), .CLOCK(clock_1_out), .CLEAR(in_1), .Read_data_1(Registradores_read_data_1),
    .Read_data_2(Registradores_read_data_2));
  assign bit_extender_1_out = {{12{1'b0}}, demultiplexer_1_out0};  // Bit_Extender bit_extender_1
  Multiplexer #(.width(16), .enable("false")) multiplexer_2 (
    .in0(bit_extender_1_out), .in1(Registradores_read_data_1), .out(multiplexer_2_out), .sel(bge));
  ULA ula_1 (
    .A(multiplexer_2_out), .B(Registradores_read_data_2), .\Função (functCtrl), .R(ula_1_r),
    .maior(ula_1_maior), .Igual(ula_1_igual));
  RAM #(.addrWidth(16), .dataWidth(16), .bus("separate")) ram_1 (
    .addr(Registradores_read_data_1), .din(Registradores_read_data_2), .data(ram_1_data),
    .str(unidadecontrole_1_memstore), .clk(clock_1_out), .ld(MemRead));  // open: sel, clr
  Multiplexer #(.enable("false")) multiplexer_3 (
    .in0(ula_1_maior), .in1(ula_1_igual), .out(multiplexer_3_out), .sel(DoI));
  Multiplexer #(.width(16), .enable("false")) multiplexer_4 (
    .in0(ram_1_data), .in1(ula_1_r), .out(WriteData), .sel(unidadecontrole_1_memorula));
  or or_1 (or_1_out, Jump, and_1_out);
  and and_1 (and_1_out, multiplexer_3_out, Branch);
  Multiplexer #(.width(16), .enable("false")) multiplexer_5 (
    .in0(adder_1_out), .in1(bit_extender_1_out), .out(multiplexer_5_out), .sel(or_1_out));

  // Notes on the sheet:
  //   contents of rom_1 (hex, n*v repeats v):
  //   770 2070 216c 771 116b 2270 3028 2020 4111 771 5004 500b
endmodule

module registradores (
  input  [3:0] Read_reg_1,
  input  [3:0] Read_reg_2,
  input  [15:0] Write_data,
  input  [3:0] Write_reg,
  input  RegWrite,
  input  CLOCK,
  input  CLEAR,
  output [15:0] Read_data_1,
  output [15:0] Read_data_2
);

  wire WE0, WE1, WE2, WE3, WE4, WE5, WE6, WE7;
  wire [15:0] demultiplexer_2_out0, demultiplexer_2_out1, demultiplexer_2_out2, demultiplexer_2_out3,
       demultiplexer_2_out4, demultiplexer_2_out5, demultiplexer_2_out6, demultiplexer_2_out7, Reg0, Reg1,
       Reg2, Reg3, Reg4, Reg5, Reg6, Reg7;

  Demultiplexer #(.select(4), .enable("false")) demultiplexer_1 (
    .out0(WE0), .out1(WE1), .out2(WE2), .out3(WE3), .out4(WE4), .out5(WE5), .out6(WE6), .out7(WE7),
    .in(RegWrite), .sel(Write_reg));  // open: out8, out9, out10, out11, out12, out13, out14, out15
  Demultiplexer #(.select(4), .width(16), .enable("false")) demultiplexer_2 (
    .out0(demultiplexer_2_out0), .out1(demultiplexer_2_out1), .out2(demultiplexer_2_out2),
    .out3(demultiplexer_2_out3), .out4(demultiplexer_2_out4), .out5(demultiplexer_2_out5),
    .out6(demultiplexer_2_out6), .out7(demultiplexer_2_out7), .in(Write_data), .sel(Write_reg));  // open: out8, out9, out10, out11, out12, out13, out14, out15
  Register #(.width(16)) t1 (.D(demultiplexer_2_out0), .en(WE0), .Q(Reg0), .clk(CLOCK), .clr(CLEAR));
  Register #(.width(16)) t2 (.D(demultiplexer_2_out1), .en(WE1), .Q(Reg1), .clk(CLOCK), .clr(CLEAR));
  Register #(.width(16)) t3 (.D(demultiplexer_2_out2), .en(WE2), .Q(Reg2), .clk(CLOCK), .clr(CLEAR));
  Register #(.width(16)) t4 (.D(demultiplexer_2_out3), .en(WE3), .Q(Reg3), .clk(CLOCK), .clr(CLEAR));
  Register #(.width(16)) t5 (.D(demultiplexer_2_out4), .en(WE4), .Q(Reg4), .clk(CLOCK), .clr(CLEAR));
  Register #(.width(16)) t6 (.D(demultiplexer_2_out5), .en(WE5), .Q(Reg5), .clk(CLOCK), .clr(CLEAR));
  Register #(.width(16)) t7 (.D(demultiplexer_2_out6), .en(WE6), .Q(Reg6), .clk(CLOCK), .clr(CLEAR));
  Register #(.width(16)) s0 (.D(demultiplexer_2_out7), .en(WE7), .Q(Reg7), .clk(CLOCK), .clr(CLEAR));
  Multiplexer #(.select(4), .width(16), .enable("false")) multiplexer_1 (
    .in0(Reg0), .in1(Reg1), .in2(Reg2), .in3(Reg3), .in4(Reg4), .in5(Reg5), .in6(Reg6), .in7(Reg7),
    .out(Read_data_1), .sel(Read_reg_1));  // open: in8, in9, in10, in11, in12, in13, in14, in15
  Multiplexer #(.select(4), .width(16), .enable("false")) multiplexer_2 (
    .in0(Reg0), .in1(Reg1), .in2(Reg2), .in3(Reg3), .in4(Reg4), .in5(Reg5), .in6(Reg6), .in7(Reg7),
    .out(Read_data_2), .sel(Read_reg_2));  // open: in8, in9, in10, in11, in12, in13, in14, in15

  // Other names for the same wires on the sheet: Read1[3:0] = Read_reg_1; Read2[3:0] = Read_reg_2
endmodule

module ULA (
  input  [15:0] A,
  input  [15:0] B,
  input  [2:0] \Função ,
  output [15:0] R,
  output maior,
  output Igual
);

  wire [15:0] AComp, adder_1_out, ADiv, AMult, ANeg, AShiftDir, AShiftEsq, ASoma, ASub, BComp, BDiv,
       bit_extender_1_out, BMult, BSoma, BSub, divider_1_out, multiplier_1_out, negator_1_out,
       subtractor_1_out, undriven;

  Demultiplexer #(.select(3), .width(16), .enable("false")) demultiplexer_1 (
    .out0(ASoma), .out1(ASub), .out2(AMult), .out3(ADiv), .out4(ANeg), .out5(AComp), .out6(AShiftEsq),
    .out7(AShiftDir), .in(A), .sel(\Função ));
  Demultiplexer #(.select(3), .width(16), .enable("false")) demultiplexer_2 (
    .out0(BSoma), .out1(BSub), .out2(BMult), .out3(BDiv), .out5(BComp), .in(B), .sel(\Função ));  // open: out4, out6, out7
  Adder #(.width(16)) adder_1 (.a(ASoma), .b(BSoma), .out(adder_1_out));  // open: cin, cout
  Subtractor #(.width(16)) subtractor_1 (.a(BSub), .b(ASub), .out(subtractor_1_out));  // open: bin, bout
  Multiplier #(.width(16)) multiplier_1 (.a(AMult), .b(BMult), .out(multiplier_1_out));  // open: cin, cout
  Divider #(.width(16)) divider_1 (.a(ADiv), .b(BDiv), .out(divider_1_out));  // open: upper, rem
  Negator #(.width(16)) negator_1 (.in(ANeg), .out(negator_1_out));
  Comparator #(.width(16)) comparator_1 (.a(AComp), .b(BComp), .gt(maior), .eq(Igual));  // open: lt
  assign bit_extender_1_out = {{15{1'b0}}, maior};  // Bit_Extender bit_extender_1
  Multiplexer #(.select(3), .width(16), .enable("false")) multiplexer_1 (
    .in0(adder_1_out), .in1(subtractor_1_out), .in2(multiplier_1_out), .in3(divider_1_out),
    .in4(negator_1_out), .in5(undriven), .in7(bit_extender_1_out), .out(R), .sel(\Função ));  // open: in6
endmodule

module UnidadeControle (
  input  a,
  input  b,
  input  c,
  input  d,
  output MemStore,
  output RegWrite,
  output MemOrULA,
  output J,
  output Branch,
  output functCtrl1,
  output functCtrl2,
  output functCtrl3,
  output MemRead,
  output li,
  output bge,
  output DestinoOuImediato
);

  wire and_1_out, and_2_out, and_3_out, and_4_out, and_5_out, and_6_out, and_7_out, and_8_out, and_9_out,
       and_10_out, and_11_out, and_12_out, and_13_out, and_14_out, and_15_out, and_16_out, not_1_out,
       not_2_out, not_3_out, not_4_out, not_5_out, not_6_out, not_7_out, not_8_out, not_9_out, not_10_out,
       not_11_out, not_12_out, not_13_out, not_14_out, not_15_out, not_16_out, not_17_out, not_18_out,
       not_19_out, not_20_out;

  and and_1 (and_1_out, b, c, d);
  not not_1 (not_1_out, d);
  and and_2 (and_2_out, b, c);
  not not_2 (not_2_out, b);
  and and_3 (and_3_out, not_2_out, d);
  not not_3 (not_3_out, b);
  and and_4 (and_4_out, not_3_out, c);
  and and_5 (and_5_out, b, not_4_out);
  not not_4 (not_4_out, d);
  and and_6 (and_6_out, b, d);
  not not_5 (not_5_out, b);
  and and_7 (and_7_out, not_5_out, d);
  and and_8 (and_8_out, c, d);
  not not_6 (not_6_out, b);
  and and_9 (and_9_out, not_6_out, d);
  not not_7 (not_7_out, c);
  and and_10 (and_10_out, b, not_7_out, not_8_out);
  not not_8 (not_8_out, d);
  and and_11 (and_11_out, b, c, d);
  not not_9 (not_9_out, b);
  and and_12 (and_12_out, not_9_out, d);
  not not_10 (not_10_out, b);
  and and_13 (and_13_out, not_10_out, not_11_out, not_12_out);
  not not_11 (not_11_out, c);
  not not_12 (not_12_out, d);
  and and_14 (and_14_out, b, c, d);
  not not_13 (not_13_out, b);
  and and_15 (and_15_out, not_13_out, not_14_out, not_15_out);
  not not_14 (not_14_out, c);
  not not_15 (not_15_out, d);
  and and_16 (and_16_out, b, c, d);
  not not_16 (not_16_out, a);
  and and_17 (bge, not_16_out, not_17_out, d);
  not not_17 (not_17_out, b);
  not not_18 (not_18_out, a);
  not not_19 (not_19_out, b);
  not not_20 (not_20_out, c);
  or or_1 (MemStore, and_1_out, a);
  or or_2 (RegWrite, not_1_out, and_2_out, a);
  or or_3 (MemOrULA, and_3_out, and_4_out, and_5_out, a);
  or or_4 (J, and_6_out, a);
  or or_5 (Branch, and_7_out, and_8_out, a);
  or or_6 (functCtrl1, and_9_out, and_10_out, a);
  or or_7 (functCtrl2, and_11_out, a);
  or or_8 (functCtrl3, and_12_out, a);
  or or_9 (MemRead, and_13_out, and_14_out, a);
  or or_10 (li, and_15_out, and_16_out, a);
  and and_18 (DestinoOuImediato, not_18_out, not_19_out, not_20_out, d);
endmodule
